# Fritzing sketch SenseBox (saved by Fritzing 1.0.6)

parts:
  Part1 = Adafruit SHT31-D [part_number="Adafruit #2857"]
  A1 = Esp32-c3 super mini
  Mod1 = CJMCU-811
  LED1 = LED - 3mm [color="Red (633nm)" current=0.030A package="3 mm [THT]"]
  Sensor1 = TTP223B Capacitive Touch Sensor Module
  J1 = Piezo Speaker

nets:
  GND: Part1.GND, A1.Pin_15, Mod1.GND, Mod1.WAK, Sensor1.GND
  VCC: Part1.VCC, A1.Pin_14, Mod1.VCC, Sensor1.VCC
  N1: Part1.SDA, A1.Pin_4, Mod1.SDA
  N2: Part1.SCL, A1.Pin_3, Mod1.SCL
  N3: A1.Pin_1, LED1.anode
  N4: A1.Pin_2, Sensor1.SIG
  N5: A1.Pin_5, J1.pin2
  N6: LED1.cathode, J1.pin1

custom parts:
  Adafruit SHT31-D: Sensirion Temperature/Humidity sensors are some of the finest & highest-accuracy devices you can get. And, finally we have some that have a true I2C interface for easy reading. The SHT31-D sensor has an excellent ±2% relative humidity and ±0.3°C accuracy for most uses. We now use the version with a PTFE filter, it'll stay clean while still allowing humidity measurements to work Unlike earlier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
  Esp32-c3 super mini: ESP32-C3 Development Board ESP32 SuperMini Development Board ESP32 Development Board WiFi Bluetooth.
  CJMCU-811: The CCS811 is an ultra-low power digital gas sensor solution which integrates a metal oxide (MOX) gas sensor to detect a wide range of Volatile Organic Compounds (VOCs) for indoor air quality monitoring with a microcontroller unit (MCU), which includes an Analog-to-Digital converter (ADC), and an I²C interface.
  TTP223B Capacitive Touch Sensor Module: The TTP223B capacitive touch sensor module uses the TTP223B IC. The appropriate voltage is approximately 2 to 5.5 volts.
